# Fritzing sketch Hardware_model (saved by Fritzing 0.9.4)

parts:
  Part1 = Arduino Nano 33 BLE Sense
  J1 = Basic Servo
  J2 = Basic Servo
  Part2 = HC-SR501 Body Sensor Module

nets:
  N1: Part1.D4, J1.pulse
  N2: Part1.D5~, J2.pulse
  N3: Part1.D6~, Part2.OUT
  GND: J2.gnd, Part2.GND
  VCC: J2.vcc, Part2.VCC

custom parts:
  Arduino Nano 33 BLE Sense: The Nano 33 BLE Sense (without headers) is Arduino’s 3.3V AI enabled board in the smallest available form factor: 45x18mm! The Arduino Nano 33 BLE Sense is a completely new board on a well-known form factor. It comes with a series of embedded sensors: 9 axis inertial sensor: what makes this board ideal for wearable devices humidity, and temperature sensor: to get highly accurate measurements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
  HC-SR501 Body Sensor Module: Pyroelectric Infrared PIR Motion Sensor Detector Module
